# Fritzing sketch LED_MQTT (saved by Fritzing 0.9.10b)
breadboards: 1

parts:
  S1 = Pushbutton [package="[THT]"]
  R1 = Resistor [tolerance=±5% power=0.25 resistance=220 package=THT]
  LED1 = LED - 3mm [color="Red (633nm)" current=0.030 package="3 mm [THT]"]
  U1 = LuaNode32_ESP32

nets:
  N1: S1.Pin_1, S1.Pin_2, U1.connector42
  N2: S1.Pin_3, S1.Pin_4, LED1.cathode, U1.connector13
  N3: R1.Pin_0, LED1.anode
  N4: R1.Pin_1, U1.connector41

notes:
  Estrutra de dados JSON:
  Ligar Led
  {
  "led": 1
  }
  Desligar Led
  {
  "led": 2
  }
